// Logisim project alu.circ as structural Verilog: 2 circuits, main circuit alu
module alu (
  input  [31:0] A,
  input  [31:0] B,
  input  [3:0] ALUSel,
  output [31:0] Result
);

  wire comparator_1_lt, comparator_2_eq, comparator_3_eq;
  wire [6:0] bitadder_1_out;
  wire [31:0] add, alu_and, bitpal, cnto, divu, mulh_1, mult, mult_1, \or , remu, sir, sll, slt, sra, srl,
       sub_1, \xor ;

  Multiplexer #(.select(4), .width(32), .enable("false")) multiplexer_1 (
    .in0(add), .in1(sub_1), .in2(mulh_1), .in3(mult), .in4(divu), .in5(remu), .in6(alu_and), .in7(\or ),
    .in8(\xor ), .in9(sll), .in10(slt), .in11(sra), .in12(srl), .in13(cnto), .in14(bitpal), .in15(sir),
    .out(Result), .sel(ALUSel));
  Adder #(.width(32)) adder_1 (.a(A), .b(B), .out(add));  // open: cin, cout
  Subtractor #(.width(32)) subtractor_1 (.a(A), .b(B), .out(sub_1));  // open: bin, bout
  Divider #(.width(32)) divider_1 (.a(A), .b(B), .out(divu), .rem(remu));  // open: upper
  assign alu_and = A & B;  // AND_Gate and_1, 32 bits wide
  assign \or  = A | B;  // OR_Gate or_1, 32 bits wide
  assign \xor  = A ^ B;  // XOR_Gate xor_1, 32 bits wide
  Multiplier #(.width(32)) multiplier_1 (.a(A), .b(B), .out(mult_1));  // open: cin, cout
  mulh u_mulh_1 (.in_1(A), .in_2(B), .out_3(mulh_1));
  Shifter #(.width(32)) shifter_1 (.in(A), .\dist (B[4:0]), .out(sll));
  Shifter #(.width(32), .shift("lr")) shifter_2 (.in(A), .\dist (B[4:0]), .out(srl));
  Comparator #(.width(32)) comparator_1 (.a(A), .b(B), .lt(comparator_1_lt));  // open: gt, eq
  BitAdder #(.width(32)) bitadder_1 (.in0(A), .in1(B), .out(bitadder_1_out));
  assign slt = {{31{comparator_1_lt}}, comparator_1_lt};  // Bit_Extender bit_extender_1
  Shifter #(.width(32), .shift("ar")) shifter_3 (.in(A), .\dist (B[4:0]), .out(sra));
  assign cnto = {{25{bitadder_1_out[6]}}, bitadder_1_out};  // Bit_Extender bit_extender_2
  Comparator #(.width(16)) comparator_2 (.a(A[15:0]), .b(A[31:16]), .eq(comparator_2_eq));  // open: gt, lt
  assign bitpal = {{31{comparator_2_eq}}, comparator_2_eq};  // Bit_Extender bit_extender_3
  Comparator #(.width(32)) comparator_3 (
    .a(A),
    .b({B[0], B[1], B[2], B[3], B[4], B[5], B[6], B[7], B[8], B[9], B[10], B[11], B[12], B[13], B[14], B[15], B[16], B[17], B[18], B[19], B[20], B[21], B[22], B[23], B[24], B[25], B[26], B[27], B[28], B[29], B[30], B[31]}),
    .eq(comparator_3_eq));  // open: gt, lt
  assign sir = {{31{comparator_3_eq}}, comparator_3_eq};  // Bit_Extender bit_extender_4

  // Notes on the sheet:
  //   INPUTS to your circuit
  //   DON'T CHANGE THE LOCATIONS OF THE INPUTS AND OUTPUTS!
  //   OUTPUT from your circuit
endmodule

module mulh (
  input  [31:0] in_1,
  input  [31:0] in_2,
  output [31:0] out_3
);

  wire Sel_1, xor_1_out;
  wire [31:0] adder_1_out, multiplexer_1_out, multiplexer_2_out, multiplexer_3_out, multiplier_1_cout,
       multiplier_1_out, negator_1_out, negator_2_out, not_1_out;

  Negator #(.width(32)) negator_1 (.in(in_1), .out(negator_1_out));
  Negator #(.width(32)) negator_2 (.in(in_2), .out(negator_2_out));
  Multiplexer #(.width(32), .enable("false")) multiplexer_1 (
    .in0(in_1), .in1(negator_1_out), .out(multiplexer_1_out), .sel(in_1[31]));
  Multiplexer #(.width(32), .enable("false")) multiplexer_2 (
    .in0(in_2), .in1(negator_2_out), .out(multiplexer_2_out), .sel(in_2[31]));
  Multiplier #(.width(32)) multiplier_1 (
    .a(multiplexer_1_out), .b(multiplexer_2_out), .out(multiplier_1_out), .cout(multiplier_1_cout));  // open: cin
  assign not_1_out = ~multiplier_1_cout;  // NOT_Gate not_1, 32 bits wide
  xor xor_1 (xor_1_out, in_1[31], in_2[31]);
  Multiplexer #(.width(32), .enable("false")) multiplexer_3 (
    .in0(multiplier_1_cout), .in1(not_1_out), .out(multiplexer_3_out), .sel(xor_1_out));
  Adder #(.width(32)) adder_1 (.a(multiplexer_3_out), .b(32'h1), .out(adder_1_out));  // open: cin, cout
  Comparator #(.width(32)) comparator_1 (.a(multiplier_1_out), .b({32{1'b0}}), .eq(Sel_1));  // open: gt, lt
  Multiplexer #(.width(32), .enable("false")) multiplexer_4 (
    .in0(multiplexer_3_out), .in1(adder_1_out), .out(out_3), .sel(Sel_1));

  // Other names for the same wires on the sheet: Neg_1 = in_1[31]; Neg_2 = in_2[31]
endmodule
