// Logisim project alu.circ as structural Verilog: 3 circuits, main circuit alu
module reverse_16bits (
  input  [15:0] in_1,
  output [15:0] out_2
);


  assign out_2 = {in_1[0], in_1[1], in_1[2], in_1[3], in_1[4], in_1[5], in_1[6], in_1[7], in_1[8], in_1[9], in_1[10], in_1[11], in_1[12], in_1[13], in_1[14], in_1[15]};
endmodule

module alu (
  input  [31:0] A,
  input  [31:0] B,
  input  [3:0] ALUSel,
  output [31:0] Result
);

  wire [0:0] output_bitpalA, output_bitpalB, output_sir, output_slt, output_slti;
  wire [6:0] output_cnto;
  wire [15:0] reverse_16bits_1_out_2, reverse_16bits_2_out_2;
  wire [31:0] adder_2_out, bit_extender_1_out, bit_extender_2_out, multiplier_3_cout, multiplier_4_out,
       multiplier_5_out, out_mulhu, output_add, output_and, output_bitpal, output_divu, output_mulh,
       output_mult, output_or, output_remu, output_sll, output_sra, output_srl, output_sub, output_xor,
       reverse_32bits_1_out_2;

  Adder #(.width(32)) adder_1 (.a(A), .b(B), .out(output_add));  // open: cin, cout
  Subtractor #(.width(32)) subtractor_1 (.a(A), .b(B), .out(output_sub));  // open: bin, bout
  Multiplier #(.width(32)) multiplier_1 (.a(A), .b(B), .out(output_mult));  // open: cin, cout
  Divider #(.width(32)) divider_1 (.a(A), .b(B), .out(output_divu));  // open: upper, rem
  Divider #(.width(32)) divider_2 (.a(A), .b(B), .rem(output_remu));  // open: out, upper
  assign output_and = A & B;  // AND_Gate and_1, 32 bits wide
  assign output_or = A | B;  // OR_Gate or_1, 32 bits wide
  assign output_xor = A ^ B;  // XOR_Gate xor_1, 32 bits wide
  Shifter #(.width(32)) shifter_1 (.in(A), .\dist (B[4:0]), .out(output_sll));
  Comparator #(.width(32), .mode("unsigned")) comparator_1 (.a(A), .b(B), .lt(output_slt[0]));  // open: gt, eq
  Shifter #(.width(32), .shift("ar")) shifter_2 (.in(A), .\dist (B[4:0]), .out(output_sra));
  Shifter #(.width(32), .shift("lr")) shifter_3 (.in(A), .\dist (B[4:0]), .out(output_srl));
  BitAdder #(.width(32)) bitadder_1 (.in0(A), .in1(B), .out(output_cnto));
  Comparator #(.width(32)) comparator_2 (.a(A), .b(B), .lt(output_slti[0]));  // open: gt, eq
  reverse_32bits reverse_32bits_1 (.in_1(B), .out_2(reverse_32bits_1_out_2));
  reverse_16bits reverse_16bits_1 (.in_1(A[15:0]), .out_2(reverse_16bits_1_out_2));
  Comparator #(.width(32)) comparator_3 (.a(A), .b(reverse_32bits_1_out_2), .eq(output_sir[0]));  // open: gt, lt
  reverse_16bits reverse_16bits_2 (.in_1(B[15:0]), .out_2(reverse_16bits_2_out_2));
  Comparator #(.width(16)) comparator_4 (
    .a(reverse_16bits_2_out_2), .b(B[31:16]), .eq(output_bitpalB[0]));  // open: gt, lt
  Multiplier #(.width(32)) multiplier_2 (.a(A), .b(B), .cout(out_mulhu));  // open: out, cin
  Comparator #(.width(16)) comparator_5 (
    .a(reverse_16bits_1_out_2), .b(A[31:16]), .eq(output_bitpalA[0]));  // open: gt, lt
  Multiplier #(.width(32)) multiplier_3 (.a(A), .b(B), .cout(multiplier_3_cout));  // open: out, cin
  assign bit_extender_1_out = {{31{B[31]}}, B[31]};  // Bit_Extender bit_extender_1
  assign bit_extender_2_out = {{31{A[31]}}, A[31]};  // Bit_Extender bit_extender_2
  assign output_bitpal = {{31{1'b0}}, output_bitpalA[0]} | {{31{1'b0}}, output_bitpalB[0]};  // OR_Gate or_2, 32 bits wide
  Multiplier #(.width(32)) multiplier_4 (.a(bit_extender_2_out), .b(B), .out(multiplier_4_out));  // open: cin, cout
  Multiplier #(.width(32)) multiplier_5 (.a(A), .b(bit_extender_1_out), .out(multiplier_5_out));  // open: cin, cout
  Multiplexer #(.select(4), .width(32), .enable("false")) multiplexer_1 (
    .in0(output_add), .in1(output_mult), .in2(output_sub), .in3(output_sll), .in4(output_mulh),
    .in5(out_mulhu), .in6({{31{1'b0}}, output_slt[0]}), .in7(output_xor), .in8(output_divu),
    .in9(output_srl), .in10(output_sra), .in11(output_or), .in12(output_remu), .in13(output_and),
    .in14({{31{1'b0}}, output_slti[0]}), .in15({{31{1'b0}}, output_sir[0]}), .out(Result), .sel(ALUSel));
  Adder #(.width(32)) adder_2 (.a(multiplier_4_out), .b(multiplier_3_cout), .out(adder_2_out));  // open: cin, cout
  Adder #(.width(32)) adder_3 (.a(adder_2_out), .b(multiplier_5_out), .out(output_mulh));  // open: cin, cout

  // Other names for the same wires on the sheet: mulh_A[31:0] = A; B_low5[4:0] = B[4:0]; mulh_B[31:0] = B

  // Notes on the sheet:
  //   INPUTS to your circuit
  //   0 add
  //   1 sub
  //   2 mulh
  //   3 mult
  //   4 divu
  //   5 remu
  //   6 and
  //   7 or
  //   8 xor
  //   9 sll
  //   10 slt
  //   11 sra
  //   12 srl
  //   13 cnto
  //   bitpal
  //   15 sir
  //   14 slti
  //   DON'T CHANGE THE LOCATIONS OF THE INPUTS AND OUTPUTS!
  //   OUTPUT from your circuit
endmodule

module reverse_32bits (
  input  [31:0] in_1,
  output [31:0] out_2
);


  assign out_2 = {in_1[0], in_1[1], in_1[2], in_1[3], in_1[4], in_1[5], in_1[6], in_1[7], in_1[8], in_1[9], in_1[10], in_1[11], in_1[12], in_1[13], in_1[14], in_1[15], in_1[16], in_1[17], in_1[18], in_1[19], in_1[20], in_1[21], in_1[22], in_1[23], in_1[24], in_1[25], in_1[26], in_1[27], in_1[28], in_1[29], in_1[30], in_1[31]};
endmodule
