// Logisim project cpu.circ as structural Verilog: 4 circuits, main circuit main
module main (
  input  [31:0] INSTRUCTION,
  input  CLOCK,
  output [31:0] FETCH_ADDRESS,
  output [31:0] ra,
  output [31:0] sp,
  output [31:0] t0,
  output [31:0] t1,
  output [31:0] t2,
  output [31:0] s0,
  output [31:0] s1,
  output [31:0] a0
);

  wire BrEq, BrLT, BrUn, BSel, MemRW, PCSel, RegWEn;
  wire [1:0] ASel, WBSel;
  wire [2:0] DataSel, ImmSel;
  wire [3:0] ALUSel;
  wire [31:0] adder_1_out, bit_extender_1_out, bit_extender_2_out, bit_extender_3_out, bit_extender_4_out,
       DMEM_p5, Inst, multiplexer_1_out, multiplexer_2_out, multiplexer_4_out, multiplexer_5_out, my_alu,
       my_Imm, my_mem, my_pc, my_pc_plus_four, my_wb, PC_Fetch_q, RegA, RegB;

  Adder #(.width(32)) adder_1 (.a(PC_Fetch_q), .b(32'h4), .out(adder_1_out));  // open: cin, cout
  Multiplexer #(.width(32), .enable("false")) multiplexer_1 (
    .in0(adder_1_out), .in1(my_alu), .out(multiplexer_1_out), .sel(PCSel));
  Multiplexer #(.width(32), .enable("false")) multiplexer_2 (
    .in0(INSTRUCTION), .in1(32'h13), .out(multiplexer_2_out), .sel(PCSel));
  Adder #(.width(32)) adder_2 (.a(my_pc), .b(32'h4), .out(my_pc_plus_four));  // open: cin, cout
  Register #(.width(32)) PC_Fetch (.D(multiplexer_1_out), .clk(CLOCK), .Q(PC_Fetch_q));  // open: en, clr
  Register #(.width(32)) Instruction_Decode (.D(multiplexer_2_out), .clk(CLOCK), .Q(Inst));  // open: en, clr
  Control control_1 (
    .Inst(Inst), .BrEQ(BrEq), .BrLT(BrLT), .PCSel(PCSel), .ImmSel(ImmSel), .BrUn(BrUn), .ASel(ASel),
    .BSel(BSel), .ALUSel(ALUSel), .MemRW(MemRW), .RegWEn(RegWEn), .out_12(DataSel), .WBSel(WBSel));
  // mem_main DMEM: pin names not known; wires that end beside it: my_alu, RegB, MemRW, CLOCK, DMEM_p5
  Register #(.width(32)) PC_Decode (.D(PC_Fetch_q), .clk(CLOCK), .Q(my_pc));  // open: en, clr
  Shifter #(.width(32), .shift("lr")) shifter_1 (.in(PC_Fetch_q), .\dist (5'b00010), .out(FETCH_ADDRESS));
  Immediate_generator immediate_generator_1 (
    .Immediate_input(Inst[31:7]), .Imm_sel_type_input(ImmSel), .Immediate_output(my_Imm));
  Branch_compare branch_compare_1 (.Reg_A(RegA), .Reg_B(RegB), .BrUn(BrUn), .BrLT(BrLT), .BrEq(BrEq));
  assign bit_extender_1_out = {{24{DMEM_p5[7]}}, DMEM_p5[7:0]};  // Bit_Extender bit_extender_1
  assign bit_extender_2_out = {{16{DMEM_p5[15]}}, DMEM_p5[15:0]};  // Bit_Extender bit_extender_2
  assign bit_extender_3_out = {{24{1'b0}}, DMEM_p5[7:0]};  // Bit_Extender bit_extender_3
  assign bit_extender_4_out = {{16{1'b0}}, DMEM_p5[15:0]};  // Bit_Extender bit_extender_4
  // Probe on ImmSel
  // Probe on ASel
  // Probe on BSel
  // Probe on MemRW
  // Probe on WBSel
  Multiplexer #(.select(3), .width(32), .enable("false")) multiplexer_3 (
    .in0(bit_extender_1_out), .in1(bit_extender_2_out), .in2(DMEM_p5), .in3(bit_extender_3_out),
    .in4(bit_extender_4_out), .out(my_mem), .sel(DataSel));  // open: in5, in6, in7
  // Probe on BrUn
  // Probe on PCSel
  // Probe on ALUSel
  // Probe on DataSel
  Multiplexer #(.width(32), .enable("false")) multiplexer_4 (
    .in0(RegB), .in1(my_Imm), .out(multiplexer_4_out), .sel(BSel));
  regfile_main RegFile (
    .rs2(Inst[24:20]), .rd(Inst[11:7]), .Read_Data_1(RegA), .Read_Data_2(RegB), .ra(ra), .sp(sp), .t0(t0),
    .t1(t1), .t2(t2), .s0(s0), .s1(s1), .a0(a0), .rs1(Inst[19:15]), .Write_Data(my_wb), .RegWEn(RegWEn),
    .clk(CLOCK));
  Multiplexer #(.select(2), .width(32), .enable("false")) multiplexer_5 (
    .in0(RegA), .in1(my_pc), .in2({32{1'b0}}), .in3(my_pc), .out(multiplexer_5_out), .sel(ASel));
  Multiplexer #(.select(2), .width(32), .enable("false")) multiplexer_6 (
    .in0(my_mem), .in1(my_alu), .in2(my_pc_plus_four), .out(my_wb), .sel(WBSel));  // open: in3
  alu Arithmetic_Logic_Unit (.A(multiplexer_5_out), .B(multiplexer_4_out), .ALUSel(ALUSel), .Result(my_alu));

  // Other names for the same wires on the sheet: clk = CLOCK; fetch_addr[31:0] = FETCH_ADDRESS; Pipe[31:0] = my_pc

  // Notes on the sheet:
  //   Fetch
  //   pipeline stage 1
  //   pipeline stage 2
  //   Decode
  //   Execute
  //   Memory
  //   Output
  //   pipeline stage 2
  //   Control
  //   Inputs/Outputs from run.circ. DO NOT MOVE THESE.
  //   pipeline stage 2
  //   Branch
  //   Inputs
  //   pipeline stage 1
  //   ALU
  //   Write Back
  //   Inputs/Outputs from run.circ. DO NOT MOVE THESE.
endmodule

module Immediate_generator (
  input  [24:0] Immediate_input,
  input  [2:0] Imm_sel_type_input,
  output [31:0] Immediate_output
);

  wire [31:0] B_type, I_type, J_type, S_type;

  assign I_type = {{20{Immediate_input[24]}}, Immediate_input[24:13]};  // Bit_Extender bit_extender_1
  assign S_type = {{20{Immediate_input[24]}}, {Immediate_input[24:18], Immediate_input[4:0]}};  // Bit_Extender bit_extender_2
  assign B_type = {{19{Immediate_input[24]}}, {Immediate_input[24], Immediate_input[0], Immediate_input[23:18], Immediate_input[4:1], 1'b0}};  // Bit_Extender bit_extender_3
  assign J_type = {{11{Immediate_input[24]}}, {Immediate_input[24], Immediate_input[12:5], Immediate_input[13], Immediate_input[23:14], 1'b0}};  // Bit_Extender bit_extender_4
  Multiplexer #(.select(3), .width(32), .enable("false")) multiplexer_1 (
    .in0(I_type), .in1(S_type), .in2(B_type), .in3({Immediate_input[24:5], {12{1'b0}}}), .in4(J_type),
    .out(Immediate_output), .sel(Imm_sel_type_input));  // open: in5, in6, in7

  // Other names for the same wires on the sheet: Imm_input[24:0] = Immediate_input;
  //   U_type[31:12] = Immediate_input[24:5]
endmodule

module Branch_compare (
  input  [31:0] Reg_A,
  input  [31:0] Reg_B,
  input  BrUn,
  output BrLT,
  output BrEq
);

  wire Signed_equal, Signed_less_than, Unsigned_equal, Unsigned_less_than;

  Multiplexer #(.enable("false")) multiplexer_1 (.in0(Signed_equal), .in1(Unsigned_equal), .out(BrEq), .sel(BrUn));
  Comparator #(.width(32)) comparator_1 (.a(Reg_A), .b(Reg_B), .eq(Signed_equal), .lt(Signed_less_than));  // open: gt
  Comparator #(.width(32), .mode("unsigned")) comparator_2 (
    .a(Reg_A), .b(Reg_B), .eq(Unsigned_equal), .lt(Unsigned_less_than));  // open: gt
  Multiplexer #(.enable("false")) multiplexer_2 (
    .in0(Signed_less_than), .in1(Unsigned_less_than), .out(BrLT), .sel(BrUn));

  // Other names for the same wires on the sheet: dataA[31:0] = Reg_A; dataB[31:0] = Reg_B

  // Notes on the sheet:
  //   signed
  //   unsigned
endmodule

module Control (
  input  [31:0] Inst,
  input  BrEQ,
  input  BrLT,
  output PCSel,
  output [2:0] ImmSel,
  output BrUn,
  output [1:0] ASel,
  output BSel,
  output [3:0] ALUSel,
  output MemRW,
  output RegWEn,
  output [2:0] out_12,
  output [1:0] WBSel
);

  wire and_1_out, comparator_10_eq, comparator_11_eq, comparator_12_eq, comparator_13_eq, comparator_14_eq,
       comparator_15_eq, comparator_16_eq, comparator_17_eq, comparator_18_eq, comparator_19_eq,
       comparator_20_eq, comparator_21_eq, comparator_22_eq, comparator_23_eq, comparator_24_eq,
       comparator_25_eq, comparator_26_eq, comparator_27_eq, comparator_28_eq, comparator_29_eq,
       comparator_30_eq, comparator_31_eq, comparator_32_eq, comparator_33_eq, demultiplexer_1_out0,
       demultiplexer_2_out0, multiplexer_2_out, not_1_out, not_2_out, or_1_out, or_2_out, or_3_out, or_6_out,
       or_7_out, or_8_out, or_9_out, or_10_out, or_11_out, or_12_out, or_13_out, wu_add, wu_addi, wu_and,
       wu_andi, wu_auipc, wu_B, wu_beq, wu_bgeu, wu_blt, wu_bltu, wu_bne, wu_divu, wu_I_load, wu_I_normal,
       wu_jal, wu_jalr, wu_lb, wu_lbu, wu_lh, wu_lhu, wu_lui, wu_lw, wu_mul, wu_mulh, wu_mulhu, wu_or,
       wu_ori, wu_R, wu_R_0, wu_R_1, wu_R_3, wu_R_5, wu_R_7, wu_remu, wu_sll, wu_slli, wu_slti, wu_sltu,
       wu_sra, wu_srl, wu_srli, wu_sub, wu_xor, wu_xori;
  wire [1:0] multiplexer_7_out, multiplexer_9_out, multiplexer_10_out;
  wire [2:0] multiplexer_1_out, multiplexer_3_out, multiplexer_4_out, multiplexer_5_out, multiplexer_25_out,
       multiplexer_26_out, multiplexer_28_out, multiplexer_29_out;
  wire [3:0] multiplexer_12_out, multiplexer_13_out, multiplexer_14_out, multiplexer_15_out,
       multiplexer_16_out, multiplexer_17_out, multiplexer_18_out, multiplexer_19_out, multiplexer_20_out,
       multiplexer_21_out, multiplexer_22_out, multiplexer_23_out, multiplexer_24_out, multiplexer_27_out;

  Multiplexer #(.width(3), .enable("false")) multiplexer_1 (
    .in0(3'b000), .in1(3'b000), .out(multiplexer_1_out), .sel(or_1_out));
  or or_1 (or_1_out, wu_I_load, wu_I_normal, wu_jalr);
  not not_1 (not_1_out, BrEQ);
  Multiplexer #(.select(3), .enable("false")) multiplexer_2 (
    .in0(BrEQ), .in1(not_1_out), .in4(BrLT), .in6(BrLT), .in7(not_2_out), .out(multiplexer_2_out),
    .sel(Inst[14:12]));  // open: in2, in3, in5
  not not_2 (not_2_out, BrLT);
  or or_2 (or_2_out, wu_jal, wu_jalr);
  Multiplexer #(.width(3), .enable("false")) multiplexer_3 (
    .in0(multiplexer_1_out), .in1(3'b001), .out(multiplexer_3_out), .sel(MemRW));
  Multiplexer #(.width(3), .enable("false")) multiplexer_4 (
    .in0(multiplexer_3_out), .in1(3'b010), .out(multiplexer_4_out), .sel(wu_B));
  and and_1 (and_1_out, wu_B, multiplexer_2_out);
  Multiplexer #(.width(3), .enable("false")) multiplexer_5 (
    .in0(multiplexer_4_out), .in1(3'b011), .out(multiplexer_5_out), .sel(or_3_out));
  Multiplexer #(.width(3), .enable("false")) multiplexer_6 (
    .in0(multiplexer_5_out), .in1(3'b100), .out(ImmSel), .sel(wu_jal));
  or or_3 (or_3_out, wu_lui, wu_auipc);
  or or_4 (RegWEn, wu_R, wu_I_load, wu_I_normal, wu_auipc, wu_jal, wu_jalr, wu_lui);
  or or_5 (PCSel, and_1_out, or_2_out);
  Multiplexer #(.width(2), .enable("false")) multiplexer_7 (
    .in0(2'b01), .in1(2'b10), .out(multiplexer_7_out), .sel(or_6_out));
  or or_6 (or_6_out, wu_jalr, wu_jal);
  or or_7 (or_7_out, wu_B, wu_jal);
  Multiplexer #(.width(2), .enable("false")) multiplexer_8 (
    .in0(multiplexer_7_out), .in1(2'b00), .out(WBSel), .sel(wu_I_load));
  Multiplexer #(.width(2), .enable("false")) multiplexer_9 (
    .in0(2'b00), .in1(2'b01), .out(multiplexer_9_out), .sel(or_7_out));
  Multiplexer #(.width(2), .enable("false")) multiplexer_10 (
    .in0(multiplexer_9_out), .in1(2'b10), .out(multiplexer_10_out), .sel(wu_lui));
  not not_3 (BSel, wu_R);
  and and_2 (BrUn, wu_B, Inst[13]);
  Multiplexer #(.width(2), .enable("false")) multiplexer_11 (
    .in0(multiplexer_10_out), .in1(2'b11), .out(ASel), .sel(wu_auipc));
  Demultiplexer #(.enable("false")) demultiplexer_1 (
    .out0(demultiplexer_1_out0), .out1(wu_mul), .in(wu_R_0), .sel(Inst[25]));
  Demultiplexer #(.enable("false")) demultiplexer_2 (
    .out0(demultiplexer_2_out0), .out1(wu_divu), .in(wu_R_5), .sel(Inst[25]));
  Multiplexer #(.width(4), .enable("false")) multiplexer_12 (
    .in0(4'b0000), .in1(4'b0000), .out(multiplexer_12_out), .sel(or_8_out));
  or or_8 (or_8_out, wu_addi, wu_add);
  Comparator #(.width(7)) comparator_1 (.a({Inst[6:2], 2'b11}), .b(7'b0000011), .eq(wu_I_load));  // open: gt, lt
  Comparator #(.width(7)) comparator_2 (.a({Inst[6:2], 2'b11}), .b(7'b0010011), .eq(wu_I_normal));  // open: gt, lt
  Comparator #(.width(7)) comparator_3 (.a({Inst[6:2], 2'b11}), .b(7'b0010111), .eq(wu_auipc));  // open: gt, lt
  Comparator #(.width(7)) comparator_4 (.a({Inst[6:2], 2'b11}), .b(7'b0100011), .eq(MemRW));  // open: gt, lt
  Comparator #(.width(7)) comparator_5 (.a({Inst[6:2], 2'b11}), .b(7'b0110011), .eq(wu_R));  // open: gt, lt
  Comparator #(.width(7)) comparator_6 (.a({Inst[6:2], 2'b11}), .b(7'b0110111), .eq(wu_lui));  // open: gt, lt
  Comparator #(.width(7)) comparator_7 (.a({Inst[6:2], 2'b11}), .b(7'b1100011), .eq(wu_B));  // open: gt, lt
  Comparator #(.width(7)) comparator_8 (.a({Inst[6:2], 2'b11}), .b(7'b1100111), .eq(wu_jalr));  // open: gt, lt
  Comparator #(.width(7)) comparator_9 (.a({Inst[6:2], 2'b11}), .b(7'b1101111), .eq(wu_jal));  // open: gt, lt
  Demultiplexer #(.enable("false")) demultiplexer_3 (
    .out0(wu_add), .out1(wu_sub), .in(demultiplexer_1_out0), .sel(Inst[30]));
  Demultiplexer #(.enable("false")) demultiplexer_4 (
    .out0(wu_srl), .out1(wu_sra), .in(demultiplexer_2_out0), .sel(Inst[30]));
  Demultiplexer #(.enable("false")) demultiplexer_5 (.out0(wu_sll), .out1(wu_mulh), .in(wu_R_1), .sel(Inst[25]));
  Demultiplexer #(.enable("false")) demultiplexer_6 (.out0(wu_sltu), .out1(wu_mulhu), .in(wu_R_3), .sel(Inst[25]));
  Demultiplexer #(.enable("false")) demultiplexer_7 (.out0(wu_and), .out1(wu_remu), .in(wu_R_7), .sel(Inst[25]));
  Multiplexer #(.width(4), .enable("false")) multiplexer_13 (
    .in0(multiplexer_12_out), .in1(4'b0001), .out(multiplexer_13_out), .sel(wu_mul));
  Multiplexer #(.width(4), .enable("false")) multiplexer_14 (
    .in0(multiplexer_13_out), .in1(4'b0010), .out(multiplexer_14_out), .sel(wu_sub));
  Multiplexer #(.width(4), .enable("false")) multiplexer_15 (
    .in0(multiplexer_14_out), .in1(4'b0011), .out(multiplexer_15_out), .sel(or_9_out));
  Multiplexer #(.width(4), .enable("false")) multiplexer_16 (
    .in0(multiplexer_15_out), .in1(4'b0100), .out(multiplexer_16_out), .sel(wu_mulh));
  or or_9 (or_9_out, wu_sll, wu_slli);
  Multiplexer #(.width(4), .enable("false")) multiplexer_17 (
    .in0(multiplexer_16_out), .in1(4'b0101), .out(multiplexer_17_out), .sel(wu_mulhu));
  Multiplexer #(.width(4), .enable("false")) multiplexer_18 (
    .in0(multiplexer_17_out), .in1(4'b0110), .out(multiplexer_18_out), .sel(wu_sltu));
  Comparator #(.width(3)) comparator_10 (.a(Inst[14:12]), .b(3'b000), .eq(comparator_10_eq));  // open: gt, lt
  Comparator #(.width(3)) comparator_11 (.a(Inst[14:12]), .b(3'b001), .eq(comparator_11_eq));  // open: gt, lt
  Comparator #(.width(3)) comparator_12 (.a(Inst[14:12]), .b(3'b010), .eq(comparator_12_eq));  // open: gt, lt
  Comparator #(.width(3)) comparator_13 (.a(Inst[14:12]), .b(3'b100), .eq(comparator_13_eq));  // open: gt, lt
  Comparator #(.width(3)) comparator_14 (.a(Inst[14:12]), .b(3'b101), .eq(comparator_14_eq));  // open: gt, lt
  Comparator #(.width(3)) comparator_15 (.a(Inst[14:12]), .b(3'b000), .eq(comparator_15_eq));  // open: gt, lt
  Comparator #(.width(3)) comparator_16 (.a(Inst[14:12]), .b(3'b001), .eq(comparator_16_eq));  // open: gt, lt
  Comparator #(.width(3)) comparator_17 (.a(Inst[14:12]), .b(3'b011), .eq(comparator_17_eq));  // open: gt, lt
  Comparator #(.width(3)) comparator_18 (.a(Inst[14:12]), .b(3'b100), .eq(comparator_18_eq));  // open: gt, lt
  Comparator #(.width(3)) comparator_19 (.a(Inst[14:12]), .b(3'b101), .eq(comparator_19_eq));  // open: gt, lt
  Comparator #(.width(3)) comparator_20 (.a(Inst[14:12]), .b(3'b110), .eq(comparator_20_eq));  // open: gt, lt
  Comparator #(.width(3)) comparator_21 (.a(Inst[14:12]), .b(3'b111), .eq(comparator_21_eq));  // open: gt, lt
  Multiplexer #(.width(4), .enable("false")) multiplexer_19 (
    .in0(multiplexer_18_out), .in1(4'b0111), .out(multiplexer_19_out), .sel(or_10_out));
  Multiplexer #(.width(4), .enable("false")) multiplexer_20 (
    .in0(multiplexer_19_out), .in1(4'b1000), .out(multiplexer_20_out), .sel(wu_divu));
  or or_10 (or_10_out, wu_xor, wu_xori);
  and and_3 (wu_lb, comparator_10_eq, wu_I_load);
  and and_4 (wu_lh, wu_I_load, comparator_11_eq);
  and and_5 (wu_lw, comparator_12_eq, wu_I_load);
  and and_6 (wu_lbu, wu_I_load, comparator_13_eq);
  and and_7 (wu_lhu, wu_I_load, comparator_14_eq);
  and and_8 (wu_R_0, comparator_15_eq, wu_R);
  and and_9 (wu_R_1, wu_R, comparator_16_eq);
  and and_10 (wu_R_3, comparator_17_eq, wu_R);
  and and_11 (wu_xor, wu_R, comparator_18_eq);
  and and_12 (wu_R_5, wu_R, comparator_19_eq);
  and and_13 (wu_or, comparator_20_eq, wu_R);
  and and_14 (wu_R_7, wu_R, comparator_21_eq);
  Multiplexer #(.width(4), .enable("false")) multiplexer_21 (
    .in0(multiplexer_20_out), .in1(4'b1001), .out(multiplexer_21_out), .sel(or_11_out));
  Multiplexer #(.width(4), .enable("false")) multiplexer_22 (
    .in0(multiplexer_21_out), .in1(4'b1010), .out(multiplexer_22_out), .sel(wu_sra));
  or or_11 (or_11_out, wu_srli, wu_srl);
  Multiplexer #(.width(4), .enable("false")) multiplexer_23 (
    .in0(multiplexer_22_out), .in1(4'b1011), .out(multiplexer_23_out), .sel(or_12_out));
  Multiplexer #(.width(4), .enable("false")) multiplexer_24 (
    .in0(multiplexer_23_out), .in1(4'b1100), .out(multiplexer_24_out), .sel(wu_remu));
  or or_12 (or_12_out, wu_or, wu_ori);
  Multiplexer #(.width(3), .enable("false")) multiplexer_25 (
    .in0(3'b000), .in1(3'b000), .out(multiplexer_25_out), .sel(wu_lb));
  Multiplexer #(.width(3), .enable("false")) multiplexer_26 (
    .in0(multiplexer_25_out), .in1(3'b001), .out(multiplexer_26_out), .sel(wu_lh));
  Multiplexer #(.width(4), .enable("false")) multiplexer_27 (
    .in0(multiplexer_24_out), .in1(4'b1101), .out(multiplexer_27_out), .sel(or_13_out));
  or or_13 (or_13_out, wu_and, wu_andi);
  Comparator #(.width(3)) comparator_22 (.a(Inst[14:12]), .b(3'b000), .eq(comparator_22_eq));  // open: gt, lt
  Comparator #(.width(3)) comparator_23 (.a(Inst[14:12]), .b(3'b001), .eq(comparator_23_eq));  // open: gt, lt
  Comparator #(.width(3)) comparator_24 (.a(Inst[14:12]), .b(3'b010), .eq(comparator_24_eq));  // open: gt, lt
  Comparator #(.width(3)) comparator_25 (.a(Inst[14:12]), .b(3'b100), .eq(comparator_25_eq));  // open: gt, lt
  Comparator #(.width(3)) comparator_26 (.a(Inst[14:12]), .b(3'b101), .eq(comparator_26_eq));  // open: gt, lt
  Comparator #(.width(3)) comparator_27 (.a(Inst[14:12]), .b(3'b110), .eq(comparator_27_eq));  // open: gt, lt
  Comparator #(.width(3)) comparator_28 (.a(Inst[14:12]), .b(3'b111), .eq(comparator_28_eq));  // open: gt, lt
  Comparator #(.width(3)) comparator_29 (.a(Inst[14:12]), .b(3'b000), .eq(comparator_29_eq));  // open: gt, lt
  Comparator #(.width(3)) comparator_30 (.a(Inst[14:12]), .b(3'b100), .eq(comparator_30_eq));  // open: gt, lt
  Comparator #(.width(3)) comparator_31 (.a(Inst[14:12]), .b(3'b110), .eq(comparator_31_eq));  // open: gt, lt
  Comparator #(.width(3)) comparator_32 (.a(Inst[14:12]), .b(3'b001), .eq(comparator_32_eq));  // open: gt, lt
  Comparator #(.width(3)) comparator_33 (.a(Inst[14:12]), .b(3'b111), .eq(comparator_33_eq));  // open: gt, lt
  Multiplexer #(.width(3), .enable("false")) multiplexer_28 (
    .in0(multiplexer_26_out), .in1(3'b010), .out(multiplexer_28_out), .sel(wu_lw));
  Multiplexer #(.width(3), .enable("false")) multiplexer_29 (
    .in0(multiplexer_28_out), .in1(3'b011), .out(multiplexer_29_out), .sel(wu_lbu));
  Multiplexer #(.width(4), .enable("false")) multiplexer_30 (
    .in0(multiplexer_27_out), .in1(4'b1110), .out(ALUSel), .sel(wu_slti));
  and and_15 (wu_addi, comparator_22_eq, wu_I_normal);
  and and_16 (wu_slli, wu_I_normal, comparator_23_eq);
  and and_17 (wu_slti, comparator_24_eq, wu_I_normal);
  and and_18 (wu_xori, wu_I_normal, comparator_25_eq);
  and and_19 (wu_srli, wu_I_normal, comparator_26_eq);
  and and_20 (wu_ori, comparator_27_eq, wu_I_normal);
  and and_21 (wu_andi, wu_I_normal, comparator_28_eq);
  and and_22 (wu_beq, comparator_29_eq, wu_B);
  and and_23 (wu_blt, wu_B, comparator_30_eq);
  and and_24 (wu_bltu, comparator_31_eq, wu_B);
  and and_25 (wu_bne, wu_B, comparator_32_eq);
  and and_26 (wu_bgeu, wu_B, comparator_33_eq);
  Multiplexer #(.width(3), .enable("false")) multiplexer_31 (
    .in0(multiplexer_29_out), .in1(3'b100), .out(out_12), .sel(wu_lhu));

  // Other names for the same wires on the sheet: ALUSel_wu[3:0] = ALUSel; ASel_wu[1:0] = ASel; BrEQ_wu = BrEQ;
  //   BrLT_wu = BrLT; BrUn_wu = BrUn; BSel_wu = BSel; DataSel[2:0] = out_12; ImmSel_wu[2:0] = ImmSel;
  //   wu_12 = Inst[12]; wu_12_14[2:0] = Inst[14:12]; wu_13 = Inst[13]; wu_14 = Inst[14]; wu_25 = Inst[25];
  //   wu_30 = Inst[30]; PCSel_wu = PCSel; RegWEn_wu = RegWEn; WBSel_wu[1:0] = WBSel; wu_2 = Inst[2];
  //   wu_2_6[4:0] = Inst[6:2]; wu_opcode[6:2] = Inst[6:2]; wu_3 = Inst[3]; wu_4 = Inst[4]; wu_5 = Inst[5];
  //   wu_6 = Inst[6]; MemRW_wu = MemRW; wu_sw = MemRW

  // Notes on the sheet:
  //   Input
  //   make outputs
  //   output
  //   Type Choice
endmodule
